# Fritzing sketch FirstRfbootProject (saved by Fritzing 0.9.3b)
breadboards: 1

parts:
  U1 = atmega328 [package=dip]
  S1 = Pushbutton [package="[SMD]"]
  HT1 = HT7333 Regulator [package=to-92-ammo]
  C1 = Ceramic Capacitor [capacitance=1µF package="100 mil [THT, multilayer]"]
  C3 = Ceramic Capacitor [capacitance=1µF package="100 mil [THT, multilayer]"]
  U2 = LIPO-110mAh [package=lipo-110]
  C4 = Ceramic Capacitor [capacitance=1µF package="100 mil [THT, multilayer]"]
  C5 = Ceramic Capacitor [capacitance=1µF package="100 mil [THT, multilayer]"]
  LED1 = LED - 3mm [color="Green (565nm)" package="3 mm [THT]"]
  R1 = Resistor [tolerance=±5% resistance=2.2k package=THT]
  D-SUN_CC1101_PINS_AT_BOTTOM = mystery part, 8 pins [chip_label=?]

nets:
  N1: U1.RESET, S1.Pin_1, S1.Pin_2
  N2: U1.D2, D-SUN_CC1101_PINS_AT_BOTTOM.pin8
  N3: U1.VCC, HT1.VOUT, C3.1, C4.0
  N4: U1.GND#7, HT1.GND, C1.0, C3.0, U2.-, C4.1
  N5: U1.D10_(PWM), D-SUN_CC1101_PINS_AT_BOTTOM.pin1
  N6: U1.D11_(PWM), D-SUN_CC1101_PINS_AT_BOTTOM.pin6
  N7: U1.D12, D-SUN_CC1101_PINS_AT_BOTTOM.pin7
  N8: U1.D13, D-SUN_CC1101_PINS_AT_BOTTOM.pin3
  N9: U1.AVCC, C5.1, D-SUN_CC1101_PINS_AT_BOTTOM.pin4
  N10: U1.GND#21, S1.Pin_3, S1.Pin_4, C5.0, R1.Pin_0, D-SUN_CC1101_PINS_AT_BOTTOM.pin5
  N11: U1.A5, LED1.anode
  N12: HT1.VIN, C1.1, U2.+
  N13: LED1.cathode, R1.Pin_1

custom parts:
  HT7333 Regulator: Voltaghe regulator 4uA qiescent current
