# Fritzing sketch usb2rf (saved by Fritzing 0.9.3b)
circuit board: 5.61484cm x 4.56394cm
breadboards: 1

parts:
  FTDI = mystery part, 18 pins [chip_label=?]
  RF = mystery part, 8 pins [chip_label=?]
  PROMINI = mystery part, 24 pins [chip_label=PROMINI]
  1u = Ceramic Capacitor [capacitance=1µF voltage=50V package="100 mil [THT, multilayer]"]
  1u_2 = Ceramic Capacitor [capacitance=1µF voltage=50V package="100 mil [THT, multilayer]"]
  U1 = mystery part, 2 pins [chip_label=?]
  U2 = mystery part, 2 pins [chip_label=?]
  U3 = mystery part, 2 pins [chip_label=?]

nets:
  N1: FTDI.pin4, PROMINI.pin17
  N2: FTDI.pin6, PROMINI.pin24
  N3: FTDI.pin9, FTDI.pin16, RF.pin1, PROMINI.pin4, PROMINI.pin23, 1u.1, 1u_2.1, U2.pin2, U3.pin1, U3.pin2
  N4: FTDI.pin10, PROMINI.pin2
  N5: FTDI.pin11, PROMINI.pin8
  N6: FTDI.pin12, PROMINI.pin20
  N7: FTDI.pin14, PROMINI.pin1
  N8: FTDI.pin15, PROMINI.pin19
  N9: FTDI.pin17, PROMINI.pin10
  N10: FTDI.pin18, PROMINI.pin9
  N11: RF.pin2, PROMINI.pin14
  N12: RF.pin3, PROMINI.pin15
  N13: RF.pin4, PROMINI.pin5
  N14: RF.pin5, PROMINI.pin13
  N15: RF.pin7, PROMINI.pin16
  N16: RF.pin8, PROMINI.pin21, 1u.0, 1u_2.0
  N17: PROMINI.pin3, PROMINI.pin6
  N18: PROMINI.pin7, U2.pin1
  N19: PROMINI.pin11, U1.pin2
  N20: PROMINI.pin12, U1.pin1

notes:
  D10
  RX TX
  GND DBG
  DEBUG
  GND GND
  USB2RF v1
